# Fritzing sketch Arduino (saved by Fritzing 0.9.3b)

parts:
  Part1 = Arduino Mega 2560 (Rev3)
  J2 = female pin header, 5 pins [form="♀ (female)"]
  Motors3and4ControlPins1 = female pin header, 4 pins [form="♀ (female)"]
  Motors1and2ControlPins2 = female pin header, 4 pins [form="♀ (female)"]
  J5 = male pin header, 4 pins [form="♂ (male)"]
  Servos = female pin header, 6 pins [form="♀ (female)"]
  MotorPotsToArduino = female pin header, 4 pins [form="♀ (female)"]
  J64 = female alternating pin header, 6 pins [form="♀ (female)"]
  SWITCHES = female pin header, 4 pins [form="♀ (female)"]
  J65 = female pin header, 5 pins [form="♀ (female)"]
  J66 = female pin header, 2 pins [form="♀ (female)"]

nets:
  Motor2AnalogOut: Part1.A1, MotorPotsToArduino.pin1
  Motor1AnalogOut: Part1.A2, MotorPotsToArduino.pin2
  Motor3AnalogOut: Part1.A3, MotorPotsToArduino.pin3
  Motor4AnalogOut: Part1.A4, MotorPotsToArduino.pin4
  AMP Switch: Part1.D12_PWM, J65.pin1
  Solo Switch: Part1.D11_PWM, J65.pin2
  Reverb Switch: Part1.D10_PWM, J65.pin3
  Ch2 and Ch3: Part1.D9_PWM, J65.pin4
  Ch1 and Ch2: Part1.D8_PWM, J65.pin5
  OVol: Part1.D2_PWM, Servos.pin6
  OTone: Part1.D3_PWM, Servos.pin5
  OGain: Part1.D4_PWM, Servos.pin4
  PVol: Part1.D5_PWM, Servos.pin3
  PTone: Part1.D6_PWM, Servos.pin2
  PGain: Part1.D7_PWM, Servos.pin1
  Amp FX Off: Part1.D22, J2.pin1
  MESA FX Off: Part1.D23, J2.pin2
  Amp Switch: Part1.D24, J2.pin3
  Bypass Off: Part1.D25, J2.pin4
  ARDUINOLEDCONTROL: Part1.D29, J64.pin1
  LEDCONTROL2: Part1.D30, J64.pin4
  LEDCONTROL4: Part1.D31, J64.pin3
  LEDCONTROL1: Part1.D32, J64.pin6
  LEDCONTROL3: Part1.D33, J64.pin5
  PanelSwitch2: Part1.D34, SWITCHES.pin2
  PanelSwitch4: Part1.D35, SWITCHES.pin1
  PanelSwitch1: Part1.D36, SWITCHES.pin4
  PanelSwitch3: Part1.D37, SWITCHES.pin3
  Motor4Input2: Part1.D38, Motors3and4ControlPins1.pin4
  Motor4Input1: Part1.D39, Motors3and4ControlPins1.pin3
  Motor3Input2: Part1.D40, Motors3and4ControlPins1.pin2
  Motor1Input2: Part1.D42, Motors1and2ControlPins2.pin4
  Motor1Input1: Part1.D43, Motors1and2ControlPins2.pin3
  Motor2Input2: Part1.D44, Motors1and2ControlPins2.pin2
  Motor2Input1: Part1.D45, Motors1and2ControlPins2.pin1
  Motor3Input1: Part1.D46, Motors3and4ControlPins1.pin1
  GndOrVolt: Part1.D48, J66.pin1
  9or-9Switch: Part1.D49, J66.pin2
  Solo: Part1.D50, J5.pin3
  OtherSwitch: Part1.D51, J5.pin4
  Ch2: Part1.D52, J5.pin1
  Ch3: Part1.D53, J5.pin2
