# Fritzing sketch AutoAmp (saved by Fritzing 0.9.3b)
stripboards: 1

parts:
  R2 = Slide Potentiometer [maximum_resistance=10kΩ]
  R3 = Slide Potentiometer [maximum_resistance=10kΩ]
  R4 = Slide Potentiometer [maximum_resistance=10kΩ]
  J9 = Basic Servo
  J10 = Basic Servo
  J11 = Basic Servo
  LED1 = LED - 5mm [color="Orange (620nm)" package="5 mm [THT]"]
  LED2 = LED - 5mm [color="Red (635nm)" package="5 mm [THT]"]
  LED3 = LED - 5mm [color="Blue (470nm)" package="5 mm [THT]"]
  J13 = female pin header, 2 pins [form="♀ (female)"]
  R5 = Resistor [tolerance=±5% resistance=220 package=THT]
  M1 = DC Motor
  IC1 = L293D [package=THT]
  Part2 = Arduino Mega 2560 (Rev3)
  IC2 = L293D [package=THT]
  J19 = female pin header, 2 pins [form="♀ (female)"]
  J20 = female pin header, 2 pins [form="♀ (female)"]
  J21 = female pin header, 2 pins [form="♀ (female)"]
  J22 = female pin header, 2 pins [form="♀ (female)"]
  JP1 = Header 2 [package=molex-1x2_lock]
  JP2 = Header 2 [package=molex-1x2_lock]
  J18 = double row female pin header, 2 pins [form="♀ (female)"]
  M2 = DC Motor
  M3 = DC Motor
  J27 = female pin header, 8 pins [form="♀ (female)"]
  J29 = male pin header, 8 pins [form="♂ (male)"]
  J30 = male pin header, 2 pins [form="♂ (male)"]
  J31 = male pin header, 2 pins [form="♂ (male)"]
  J32 = male pin header, 2 pins [form="♂ (male)"]
  J33 = female pin header, 3 pins [form="♀ (female)"]
  J34 = female pin header, 3 pins [form="♀ (female)"]
  J35 = female pin header, 6 pins [form="♀ (female)"]
  J14 = male pin header, 4 pins [form="♂ (male)"]
  J12 = female pin header, 4 pins [form="♀ (female)"]
  S1 = Round Pushbutton
  S2 = Round Pushbutton
  S3 = Round Pushbutton
  S4 = Round Pushbutton
  S5 = Round Pushbutton
  J36 = male pin header, 6 pins [form="♂ (male)"]
  M4 = DC Motor  # not connected
  R6 = Slide Potentiometer [maximum_resistance=10kΩ]
  J8 = single row smd male pin header, 4 pins [form="♂ (male)"]

nets:
  N1: R2.leg1, R3.leg1, R4.leg1, J13.pin1, R6.leg1
  N2: R2.wiper, J8.pin3
  N3: R2.leg2, R3.leg2, R6.leg2
  N4: R3.wiper, J8.pin2
  N5: R4.wiper, J8.pin1
  N6: R4.leg2, J13.pin2
  GND: J9.gnd, J10.gnd, J11.gnd
  VCC: J9.vcc, J10.vcc, J11.vcc
  N7: J9.pulse, J34.pin1
  N8: J10.pulse, J34.pin2
  N9: J11.pulse, J34.pin3
  N10: LED1.cathode, LED2.cathode, LED3.cathode, R5.Pin_1
  N11: LED1.anode, J12.pin2
  N12: LED2.anode, J12.pin1
  N13: LED3.anode, J12.pin3
  N14: R5.Pin_0, J12.pin4
  N15: M1.pin_1, J32.pin1
  N16: M1.pin_2, J32.pin2
  N17: IC1.Enable_1, IC1.Enable_2, IC1.+V, Part2.5V, IC2.Enable_1, IC2.+V, JP1.1, J18.pin1
  N18: IC1.In_1, J27.pin4
  N19: IC1.Out_1_(_Controlled_by_Enable_1_), J19.pin1
  GND_2: IC1.0V, Part2.GND, IC2.0V, JP1.2, J18.pin2, J35.pin6, J14.pin4
  N20: IC1.Out_2_(_Controlled_by_Enable_1_), J19.pin2
  N21: IC1.In_2, J27.pin5
  N22: IC1.+Vmotor, IC2.+Vmotor, JP2.1
  N23: IC1.In_3, J27.pin8
  N24: IC1.Out_3_(_Controlled_by_Enable_2_), J21.pin2
  N25: IC1.Out_4_(_Controlled_by_Enable_2_), J21.pin1
  N26: IC1.In_4, J27.pin1
  N27: Part2.D21/SCL, J33.pin1
  N28: Part2.D20/SDA, J33.pin2
  N29: Part2.D19/RX1, J33.pin3
  N30: Part2.D16_PWM/TX2, J14.pin3
  N31: Part2.D15/RX3, J14.pin2
  N32: Part2.D14/TX3, J14.pin1
  N33: Part2.D22, J29.pin1
  N34: Part2.D23, J29.pin8
  N35: Part2.D24, J29.pin2
  N36: Part2.D25, J29.pin7
  N37: Part2.D26, J29.pin3
  N38: Part2.D27, J29.pin6
  N39: Part2.D28, J29.pin4
  N40: Part2.D29, J29.pin5
  N41: Part2.D45, J35.pin1
  N42: Part2.D47, J35.pin2
  N43: Part2.D49, J35.pin3
  N44: Part2.D51, J35.pin4
  N45: Part2.D53, J35.pin5
  N46: IC2.In_1, J27.pin3
  N47: IC2.Out_1_(_Controlled_by_Enable_1_), J20.pin1
  N48: IC2.Out_2_(_Controlled_by_Enable_1_), J20.pin2
  N49: IC2.In_2, J27.pin6
  N50: IC2.In_3, J27.pin7
  N51: IC2.Out_3_(_Controlled_by_Enable_2_), J22.pin2
  N52: IC2.Out_4_(_Controlled_by_Enable_2_), J22.pin1
  N53: IC2.In_4, J27.pin2
  N54: M2.pin_1, J31.pin1
  N55: M2.pin_2, J31.pin2
  N56: M3.pin_1, J30.pin1
  N57: M3.pin_2, J30.pin2
  N58: S1.leg0, J36.pin6
  N59: S1.leg1, S2.leg1, S3.leg1, S4.leg1, S5.leg1, J36.pin1
  N60: S2.leg0, J36.pin5
  N61: S3.leg0, J36.pin4
  N62: S4.leg0, J36.pin3
  N63: S5.leg0, J36.pin2
  N64: R6.wiper, J8.pin4
