# Fritzing sketch FootSwitch (saved by Fritzing 0.9.3b)
stripboards: 4
breadboards: 1

parts:
  Solo_LED = LED - 5mm [color="Red (633nm)" package="5 mm [THT]"]
  Solo_Switch = Toggle Switch [package=THT]
  Ch2_LED = LED - 5mm [color="Orange (620nm)" package="5 mm [THT]"]
  Ch1_LED = LED - 5mm [color="Blue (525nm)" package="5 mm [THT]"]
  Amp_Switch = SWITCH-DPDT [package=gpi-152-3013]
  Jack = female pin header, 8 pins [form="♀ (female)"]
  AMP_LED = RGB LED (com. cathode, rgb) [package="5 mm [THT]"]
  Ch3 = SWITCH-DPDT [package=gpi-152-3013]
  Ch2 = SWITCH-DPDT [package=gpi-152-3013]
  Ch1 = SWITCH-DPDT [package=gpi-152-3013]
  Reverb_Switch = Toggle Switch [package=THT]
  Solo_LED1 = LED - 5mm [color="Blue (505nm)" package="5 mm [THT]"]
  J1 = female pin header, 5 pins [form="♀ (female)"]
  J2 = female pin header, 2 pins [form="♀ (female)"]
  Ch3_LED = LED - 5mm [color="Red (633nm)" package="5 mm [THT]"]
  J3 = female pin header, 2 pins [form="♀ (female)"]
  J4 = female pin header, 2 pins [form="♀ (female)"]
  J5 = female pin header, 3 pins [form="♀ (female)"]
  J6 = female pin header, 3 pins [form="♀ (female)"]
  J7 = female pin header, 2 pins [form="♀ (female)"]
  J8 = female pin header, 2 pins [form="♀ (female)"]
  J9 = female pin header, 2 pins [form="♀ (female)"]
  J10 = female pin header, 2 pins [form="♀ (female)"]
  J11 = female pin header, 2 pins [form="♀ (female)"]
  J12 = female pin header, 2 pins [form="♀ (female)"]
  J13 = female pin header, 3 pins [form="♀ (female)"]
  R6 = Resistor [tolerance=±5% resistance=220 package=THT]
  R7 = Resistor [tolerance=±10% resistance=220 package=THT]
  R8 = Resistor [tolerance=±5% resistance=220 package=THT]
  J16 = female pin header, 3 pins [form="♀ (female)"]
  J17 = female pin header, 3 pins [form="♀ (female)"]
  J18 = female pin header, 3 pins [form="♀ (female)"]
  J15 = male pin header, 5 pins [form="♂ (male)"]
  D5 = Rectifier Diode [part_number=1N4001 package="300 mil [THT]"]
  Q5 = PNP-Transistor [package="TO92 [THT]"]
  R20 = Resistor [tolerance=±5% resistance=47k package=THT]
  R21 = Resistor [tolerance=±5% resistance=1k package=THT]
  R22 = Resistor [tolerance=±5% resistance=220 package=THT]
  R23 = Resistor [tolerance=±5% resistance=220 package=THT]
  Q6 = PNP-Transistor [package="TO92 [THT]"]
  R24 = Resistor [tolerance=±5% resistance=10k package=THT]
  R25 = Resistor [tolerance=±5% resistance=220 package=THT]
  R26 = Resistor [tolerance=±5% resistance=10k package=THT]
  Q7 = NPN-Transistor [package="TO92 [THT]"]
  U6 = TLP621 [package=THT]
  D6 = Rectifier Diode [part_number=1N4001 package="300 mil [THT]"]
  D3 = Rectifier Diode [part_number=1N4001 package="300 mil [THT]"]
  D4 = Rectifier Diode [part_number=1N4001 package="300 mil [THT]"]
  R19 = Resistor [tolerance=±5% resistance=220 package=THT]
  Jack_2 = female pin header, 9 pins [form="♀ (female)"]
  R27 = Resistor [tolerance=±5% resistance=220 package=THT]
  U7 = 941H-2C-5D [package=relay-5v]
  U8 = 941H-2C-5D [package=relay-5v]
  R28 = Resistor [tolerance=±5% resistance=220 package=THT]
  R29 = Resistor [tolerance=±5% resistance=220 package=THT]
  R30 = Resistor [tolerance=±5% resistance=220 package=THT]
  R31 = Resistor [tolerance=±5% resistance=220 package=THT]
  R32 = Resistor [tolerance=±5% resistance=220 package=THT]
  J19 = female pin header, 2 pins [form="♀ (female)"]
  J20 = female pin header, 2 pins [form="♀ (female)"]
  J21 = female pin header, 3 pins [form="♀ (female)"]

nets:
  GND: Solo_LED.cathode, Ch2_LED.cathode, Ch1_LED.cathode, Jack.pin8, AMP_LED.common_cathode, Solo_LED1.cathode, Ch3_LED.cathode, J5.pin1, J6.pin1, J7.pin1, J8.pin1, J9.pin2, J10.pin1, J11.pin1, J12.pin1, J13.pin1, J16.pin1, J15.pin1, D5.cathode, R20.Pin_0, D4.anode, Jack_2.pin8, Jack_2.pin9, U7.1, U8.1, U8.9, R28.Pin_0, R29.Pin_0, R30.Pin_0, R31.Pin_0, R32.Pin_0, J19.pin2
  N1: Solo_LED.anode, Solo_Switch.L2, J7.pin2
  N2: Solo_Switch.L1, J17.pin2, J18.pin2, Jack_2.pin4, J21.pin2
  N3: Solo_Switch.COM, R6.Pin_0
  N4: Ch2_LED.anode, J11.pin2, J13.pin3, J16.pin3, R23.Pin_0
  N5: Ch1_LED.anode, Ch3_LED.anode, J10.pin2, J12.pin2, J13.pin2, J16.pin2, R22.Pin_0, R25.Pin_0
  N6: Amp_Switch.2, R8.Pin_0
  Variable Power: Amp_Switch.5, Ch3.3, Ch2.3, Ch2.6, Ch1.3, J9.pin1, R6.Pin_1, R7.Pin_1, R8.Pin_1, Jack_2.pin1, R27.Pin_0
  N7: Amp_Switch.1, AMP_LED.red_anode, AMP_LED.green_anode, J5.pin2, J6.pin2
  N8: Amp_Switch.3, AMP_LED.blue_anode, J5.pin3, J6.pin3
  N9: Amp_Switch.6, J17.pin1, J18.pin1, Jack_2.pin3, J21.pin3
  N10: Jack.pin1, J15.pin3
  N11: Jack.pin2, U8.13
  N12: Jack.pin3, J1.pin1, R32.Pin_1
  N13: Jack.pin4, J1.pin2, R31.Pin_1
  N14: Jack.pin5, J1.pin3, R30.Pin_1
  N15: Jack.pin6, J1.pin4, R29.Pin_1
  N16: Jack.pin7, J1.pin5, R28.Pin_1
  N17: Ch3.5, Ch2.5, J3.pin2, J4.pin2, Jack_2.pin6, J20.pin2
  N18: Ch2.2, Ch1.2, J3.pin1, J4.pin1, Jack_2.pin7, J20.pin1
  N19: Reverb_Switch.L1, J17.pin3, J18.pin3, Jack_2.pin5, J21.pin1
  N20: Reverb_Switch.COM, R7.Pin_0
  N21: Reverb_Switch.L2, Solo_LED1.anode, J8.pin2
  GndOrVolt: J2.pin1, U8.16
  9or-9Switch: J2.pin2, U7.16
  N22: J15.pin2, U7.11
  N23: J15.pin4, U7.9
  N24: D5.anode, D6.anode, R19.Pin_0
  Variable Power Post: Q5.E, U6.Pin_4, R27.Pin_1, J19.pin1
  N25: Q5.B, R20.Pin_1, R21.Pin_0
  N26: Q5.C, R22.Pin_1
  PostCouplerPWR: R21.Pin_1, Q6.E, Q7.C, U6.Pin_3
  N27: R23.Pin_1, Q6.C
  N28: Q6.B, R24.Pin_0
  LEDCNTRL: R24.Pin_1, R26.Pin_1, D6.cathode, D3.anode, Jack_2.pin2
  N29: R25.Pin_1, Q7.E
  N30: R26.Pin_0, Q7.B
  N31: U6.Pin_1, D3.cathode, D4.cathode
  N32: U6.Pin_2, R19.Pin_1
  N33: U7.13, U8.11

custom parts:
  941H-2C-5D: DPDT Relay - 2 Form C
