# Fritzing sketch FootSwitch3-alt (saved by Fritzing 0.9.3b)
stripboards: 3

parts:
  Solo_LED = LED - 5mm [color="Red (633nm)" package="5 mm [THT]"]
  Solo_Switch = Toggle Switch [package=THT]
  Ch2_LED = LED - 5mm [color="Orange (620nm)" package="5 mm [THT]"]
  Ch1_LED = LED - 5mm [color="Blue (525nm)" package="5 mm [THT]"]
  Amp_Switch = SWITCH-DPDT [package=gpi-152-3013]
  Ethernet_Jack = female pin header, 8 pins [form="♀ (female)"]
  Ethernet_Jack2 = female pin header, 8 pins [form="♀ (female)"]
  U1 = 941H-2C-5D [package=relay-5v]
  U2 = 941H-2C-5D [package=relay-5v]
  U3 = 941H-2C-5D [package=relay-5v]
  AMP_LED = RGB LED (com. cathode, rgb) [package="5 mm [THT]"]
  IC1 = IC, DIP package, 8 pins [chip_label=IC]
  D1 = Rectifier Diode [part_number=1N4001 package="300 mil [THT]"]
  D2 = Rectifier Diode [part_number=1N4001 package="300 mil [THT]"]
  C1 = Electrolytic Capacitor [capacitance=1µF package="100 mil [THT, electrolytic]"]
  C2 = Electrolytic Capacitor [capacitance=1µF package="100 mil [THT, electrolytic]"]
  C3 = Electrolytic Capacitor [capacitance=1µF package="100 mil [THT, electrolytic]"]
  C4 = Electrolytic Capacitor [capacitance=1µF package="100 mil [THT, electrolytic]"]
  Ch3 = SWITCH-DPDT [package=gpi-152-3013]
  Ch2 = SWITCH-DPDT [package=gpi-152-3013]
  Ch1 = SWITCH-DPDT [package=gpi-152-3013]
  Reverb_Switch = Toggle Switch [package=THT]
  Solo_LED1 = LED - 5mm [color="Blue (505nm)" package="5 mm [THT]"]
  J1 = female pin header, 5 pins [form="♀ (female)"]
  J2 = female pin header, 2 pins [form="♀ (female)"]
  Ch3_LED = LED - 5mm [color="Red (633nm)" package="5 mm [THT]"]
  J3 = female pin header, 2 pins [form="♀ (female)"]  # not connected
  J4 = female pin header, 2 pins [form="♀ (female)"]  # not connected
  J5 = female pin header, 3 pins [form="♀ (female)"]  # not connected
  J6 = female pin header, 3 pins [form="♀ (female)"]  # not connected
  J7 = female pin header, 2 pins [form="♀ (female)"]  # not connected
  J8 = female pin header, 2 pins [form="♀ (female)"]  # not connected
  J9 = female pin header, 2 pins [form="♀ (female)"]  # not connected
  J10 = female pin header, 2 pins [form="♀ (female)"]  # not connected
  J11 = female pin header, 2 pins [form="♀ (female)"]  # not connected
  J12 = female pin header, 2 pins [form="♀ (female)"]  # not connected
  J13 = female pin header, 3 pins [form="♀ (female)"]  # not connected
  J14 = female pin header, 3 pins [form="♀ (female)"]
  J15 = male pin header, 3 pins [form="♂ (male)"]
  Power_plug1 = Power plug
  R2 = Resistor [tolerance=±5% resistance=220 package=THT]
  R1 = Resistor [tolerance=±5% resistance=220 package=THT]
  R6 = Resistor [tolerance=±5% resistance=220 package=THT]
  R7 = Resistor [tolerance=±5% resistance=220 package=THT]
  R8 = Resistor [tolerance=±5% resistance=220 package=THT]
  IC2 = Dual Op-Amp [package=dip08]
  R9 = Rotary Potentiometer (Large) [maximum_resistance=100kΩ package=THT]
  R10 = Resistor [tolerance=±5% resistance=47k package=THT]
  R11 = Resistor [tolerance=±5% resistance=47k package=THT]

nets (from the schematic view):
  N1: Solo_LED.cathode, Ch2_LED.cathode, Ch1_LED.anode, Ethernet_Jack.pin8, AMP_LED.common_cathode, Solo_LED1.cathode, Ch3_LED.cathode
  N2: Solo_LED.anode, Solo_Switch.L2
  N3: Solo_Switch.L1, Ethernet_Jack.pin4
  N4: Solo_Switch.COM, R6.Pin_0
  N5: Ch2_LED.anode, R2.Pin_1
  N6: Ch1_LED.cathode, Ch3_LED.anode, R1.Pin_0
  N7: Amp_Switch.2, R8.Pin_0
  N8: Amp_Switch.5, Ethernet_Jack.pin1, U1.6, Ch3.3, Ch2.3, Ch2.6, Ch1.3, R6.Pin_1, R7.Pin_1, R8.Pin_1
  N9: Amp_Switch.1, AMP_LED.red_anode, AMP_LED.green_anode
  N10: Amp_Switch.3, AMP_LED.blue_anode
  N11: Amp_Switch.6, Ethernet_Jack.pin3
  N12: Ethernet_Jack.pin2, U1.1
  N13: Ethernet_Jack.pin5, Reverb_Switch.L1
  N14: Ethernet_Jack.pin6, Ch3.5, Ch2.5
  N15: Ethernet_Jack.pin7, Ch2.2, Ch1.2
  N16: Ethernet_Jack2.pin1, U2.9, J15.pin3
  N17: Ethernet_Jack2.pin2, U3.11
  N18: Ethernet_Jack2.pin3, J1.pin1
  N19: Ethernet_Jack2.pin4, J1.pin2
  N20: Ethernet_Jack2.pin5, J1.pin3
  N21: Ethernet_Jack2.pin6, J1.pin4
  N22: Ethernet_Jack2.pin7, J1.pin5
  N23: Ethernet_Jack2.pin8, U2.1, U3.1, J15.pin1
  N24: U1.4, U1.13
  N25: U1.8, U1.16
  N26: U1.9, R1.Pin_1
  N27: U1.11, R2.Pin_0
  N28: U2.11, J15.pin2
  N29: U2.13, U3.13
  N30: U2.16, J2.pin2
  N31: U3.16, J2.pin1
  9V: IC1.pin1, IC1.pin8, D2.anode, J14.pin3, Power_plug1.VCC, IC2.A_V-, R10.Pin_0
  N32: IC1.pin2, C2.+, C3.-
  GND: IC1.pin3, C1.-, C4.-, J14.pin1, Power_plug1.GND, IC2.A_V+, R11.Pin_1
  N33: IC1.pin4, C2.-
  -9V: IC1.pin5, C4.+, J14.pin2
  18V: D1.cathode, C1.+
  N34: D1.anode, D2.cathode, C3.+
  N35: Reverb_Switch.COM, R7.Pin_0
  N36: Reverb_Switch.L2, Solo_LED1.anode
  N37: IC2.A_OUT, IC2.A_-IN
  N38: IC2.A_+IN, R9.wiper
  N39: R9.leg1, R10.Pin_1
  N40: R9.leg2, R11.Pin_0

custom parts:
  941H-2C-5D: DPDT Relay - 2 Form C
