# Fritzing sketch FootSwitch4 (saved by Fritzing 0.9.3b)
stripboards: 4
breadboards: 1

parts:
  Solo_LED = LED - 5mm [color="Red (633nm)" package="5 mm [THT]"]
  Solo_Switch = Toggle Switch [package=THT]
  Ch2_LED = LED - 5mm [color="Orange (620nm)" package="5 mm [THT]"]
  Ch1_LED = LED - 5mm [color="Blue (525nm)" package="5 mm [THT]"]
  Amp_Switch = SWITCH-DPDT [package=gpi-152-3013]
  Ethernet_Jack = female pin header, 8 pins [form="♀ (female)"]
  Ethernet_Jack2 = female pin header, 8 pins [form="♀ (female)"]
  AMP_LED = RGB LED (com. cathode, rgb) [package="5 mm [THT]"]
  IC1 = IC, DIP package, 8 pins [chip_label=IC]
  C2 = Electrolytic Capacitor [capacitance=1µF package="100 mil [THT, electrolytic]"]
  Ch3 = SWITCH-DPDT [package=gpi-152-3013]
  Ch2 = SWITCH-DPDT [package=gpi-152-3013]
  Ch1 = SWITCH-DPDT [package=gpi-152-3013]
  Reverb_Switch = Toggle Switch [package=THT]
  Solo_LED1 = LED - 5mm [color="Blue (505nm)" package="5 mm [THT]"]
  J1 = female pin header, 5 pins [form="♀ (female)"]
  J2 = female pin header, 2 pins [form="♀ (female)"]
  Ch3_LED = LED - 5mm [color="Red (633nm)" package="5 mm [THT]"]
  J3 = female pin header, 2 pins [form="♀ (female)"]
  J4 = female pin header, 2 pins [form="♀ (female)"]
  J5 = female pin header, 3 pins [form="♀ (female)"]
  J6 = female pin header, 3 pins [form="♀ (female)"]
  J7 = female pin header, 2 pins [form="♀ (female)"]
  J8 = female pin header, 2 pins [form="♀ (female)"]
  J9 = female pin header, 2 pins [form="♀ (female)"]
  J10 = female pin header, 2 pins [form="♀ (female)"]
  J11 = female pin header, 2 pins [form="♀ (female)"]
  J12 = female pin header, 2 pins [form="♀ (female)"]
  J13 = female pin header, 3 pins [form="♀ (female)"]
  R2 = Resistor [tolerance=±5% resistance=220 package=THT]
  R6 = Resistor [tolerance=±5% resistance=220 package=THT]
  R7 = Resistor [tolerance=±10% resistance=220 package=THT]
  R8 = Resistor [tolerance=±5% resistance=220 package=THT]
  J16 = female pin header, 3 pins [form="♀ (female)"]
  J17 = female pin header, 3 pins [form="♀ (female)"]
  J18 = female pin header, 3 pins [form="♀ (female)"]
  J19 = female pin header, 2 pins [form="♀ (female)"]
  IC3 = Dual Op-Amp [package=dip08]
  R13 = Resistor [tolerance=±10% resistance=4.7k package=THT]
  R14 = Resistor [tolerance=±5% resistance=4.7k package=THT]
  R12 = Rotary Potentiometer (Large) [maximum_resistance=10kΩ package=THT]
  C6 = Electrolytic Capacitor [capacitance=1µF package="100 mil [THT, electrolytic]"]
  J15 = male pin header, 5 pins [form="♂ (male)"]
  U1 = 941H-2C-5D [package=relay-5v]
  U2 = 941H-2C-5D [package=relay-5v]
  U3 = 941H-2C-5D [package=relay-5v]
  IC4 = IC, DIP package, 8 pins [chip_label=IC]
  C7 = Electrolytic Capacitor [capacitance=1µF package="100 mil [THT, electrolytic]"]
  J20 = female pin header, 2 pins [form="♀ (female)"]
  J14 = female pin header, 4 pins [form="♀ (female)"]
  R1 = Resistor [tolerance=±10% resistance=68 package=THT]
  Q3 = PNP-Transistor [package="TO92 [THT]"]
  Q4 = NPN-Transistor [package="TO92 [THT]"]
  D1 = Rectifier Diode [part_number=1N4001 package="300 mil [THT]"]
  D2 = Rectifier Diode [part_number=1N4001 package="300 mil [THT]"]
  D3 = Rectifier Diode [part_number=1N4001 package="300 mil [THT]"]
  R17 = Rotary Potentiometer (Large) [maximum_resistance=10kΩ package=THT]
  R18 = Resistor [tolerance=±5% resistance=330 package=THT]

nets (from the breadboard view):
  N1: Solo_LED.cathode, Ch2_LED.cathode, Ch1_LED.anode, Ethernet_Jack.pin8, AMP_LED.common_cathode, Solo_LED1.cathode, Ch3_LED.cathode, J5.pin1, J6.pin1, J7.pin1, J8.pin1, J9.pin2, J10.pin1, J11.pin1, J12.pin1, J13.pin1, J16.pin1, J19.pin1, R1.Pin_0
  N2: Solo_LED.anode, Solo_Switch.L2, J7.pin2
  N3: Solo_Switch.L1, Ethernet_Jack.pin4, J17.pin2, J18.pin2
  N4: Solo_Switch.COM, R6.Pin_0
  N5: Ch2_LED.anode, J11.pin2, J13.pin3, R2.Pin_1, J16.pin3
  N6: Ch1_LED.cathode, Ch3_LED.anode, J10.pin2, J12.pin2, J13.pin2, J16.pin2, U1.16, R1.Pin_1
  N7: Amp_Switch.2, R8.Pin_0
  N8: Amp_Switch.5, Ethernet_Jack.pin1, Ch3.3, Ch2.3, Ch2.6, Ch1.3, J9.pin1, R6.Pin_1, R7.Pin_1, R8.Pin_1, J19.pin2, U1.11
  N9: Amp_Switch.1, AMP_LED.red_anode, AMP_LED.green_anode, J5.pin2, J6.pin2
  N10: Amp_Switch.3, AMP_LED.blue_anode, J5.pin3, J6.pin3
  N11: Amp_Switch.6, Ethernet_Jack.pin3, J17.pin1, J18.pin1
  N12: Ethernet_Jack.pin2, U1.1
  N13: Ethernet_Jack.pin5, Reverb_Switch.L1, J17.pin3, J18.pin3
  N14: Ethernet_Jack.pin6, Ch3.5, Ch2.5, J3.pin2, J4.pin2
  N15: Ethernet_Jack.pin7, Ch2.2, Ch1.2, J3.pin1, J4.pin1
  N16: Ethernet_Jack2.pin1, J15.pin3
  N17: Ethernet_Jack2.pin2, U2.13
  N18: Ethernet_Jack2.pin3, J1.pin1
  N19: Ethernet_Jack2.pin4, J1.pin2
  N20: Ethernet_Jack2.pin5, J1.pin3
  N21: Ethernet_Jack2.pin6, J1.pin4
  N22: Ethernet_Jack2.pin7, J1.pin5
  N23: Ethernet_Jack2.pin8, J15.pin1, U2.1, U2.9, U3.1, R17.leg1
  N24: IC1.pin2, C2.+
  N25: IC1.pin3, IC3.A_V-, R14.Pin_1, C6.+, IC4.pin3, J20.pin2, J14.pin1
  N26: IC1.pin4, C2.-
  N27: IC1.pin5, C6.-, IC4.pin5, J14.pin2
  N28: IC1.pin8, IC3.A_V+, R13.Pin_0, IC4.pin8, J20.pin1, J14.pin4
  N29: Reverb_Switch.COM, R7.Pin_0
  N30: Reverb_Switch.L2, Solo_LED1.anode, J8.pin2
  N31: J2.pin1, U2.16
  N32: J2.pin2, U3.16
  N33: R2.Pin_0, U1.13
  N34: IC3.A_OUT, IC3.A_-IN, J14.pin3
  N35: IC3.A_+IN, R12.wiper
  N36: R13.Pin_1, R12.leg2
  N37: R14.Pin_0, R12.leg1
  N38: J15.pin2, U3.11
  N39: J15.pin4, U3.9
  N40: U2.11, Q3.C, Q4.C
  N41: U3.13, Q4.E, D1.anode, R18.Pin_0
  N42: IC4.pin2, C7.+
  N43: IC4.pin4, C7.-
  N44: Q3.E, D1.cathode
  N45: Q3.B, D3.anode
  N46: Q4.B, D2.cathode
  N47: D2.anode, D3.cathode, R17.wiper
  N48: R17.leg2, R18.Pin_1

custom parts:
  941H-2C-5D: DPDT Relay - 2 Form C
