# Fritzing sketch InputStage (saved by Fritzing 0.9.3b)

parts:
  U4 = 941H-2C-5D [package=relay-5v]
  Master_Input = Stereo Jack (TRS) 3.5mm [package="PG203J [THT]"]
  ToMesaInput = Stereo Jack (TRS) 3.5mm [package="PG203J [THT]"]  # not connected

nets:
  N1: U4.4, Master_Input.Ring

custom parts:
  941H-2C-5D: DPDT Relay - 2 Form C
