# Fritzing sketch FootSwitch (saved by Fritzing 0.9.3b)
stripboards: 1

parts:
  LED2 = LED - 5mm [color="Red (633nm)" package="5 mm [THT]"]
  LED3 = LED - 5mm [color="Red (633nm)" package="5 mm [THT]"]
  U1 = RJ45 Jack [package=rj45-8]
  S1 = Toggle Switch [package=THT]
  S2 = Toggle Switch [package=THT]
  S3 = Toggle Switch [package=THT]
  S4 = Toggle Switch [package=THT]
  K1 = Relay [part_number=FRS1B-S package=THT]
  LED5 = LED - 5mm [color="Red (633nm)" package="5 mm [THT]"]
  LED4 = LED - 5mm [color="Red (633nm)" package="5 mm [THT]"]
  K2 = Relay [part_number=FRS1B-S package=THT]
  LED6 = LED - 5mm [color="Red (633nm)" package="5 mm [THT]"]
  S7 = SWITCH-DPDT [package=gpi-152-3013]
  LED7 = LED - 5mm [color="Red (633nm)" package="5 mm [THT]"]

nets:
  GND: LED2.cathode, U1.8, S1.L2, S2.L2, S3.L2, S4.COM, K1.COIL1, LED4.cathode, K2.COIL1, LED6.anode, S7.2, S7.5
  N1: LED2.anode, K1.A, LED6.cathode
  N2: LED3.cathode, S4.L1
  N3: LED3.anode, U1.1, K2.B
  N4: U1.2, K1.COIL2, K2.A, K2.COIL2
  N5: U1.3, S7.6
  N6: U1.4, S4.L2
  N7: U1.5, S3.COM
  N8: U1.6, S2.COM
  N9: U1.7, S1.COM
  N10: K1.C2, K2.C1, K2.C2
  N11: K1.B, LED4.anode
  N12: LED5.cathode, S7.1
  N13: LED5.anode, LED7.anode
  N14: S7.3, LED7.cathode
