# Fritzing sketch FootSwitch2 (saved by Fritzing 0.9.3b)
stripboards: 1

parts:
  LED2 = LED - 5mm [color="Red (633nm)" package="5 mm [THT]"]
  LED3 = LED - 5mm [color="Red (633nm)" package="5 mm [THT]"]
  S1 = Toggle Switch [package=THT]
  S2 = Toggle Switch [package=THT]
  S3 = Toggle Switch [package=THT]
  S4 = Toggle Switch [package=THT]
  K1 = Relay [part_number=FRS1B-S package=THT]
  LED5 = LED - 5mm [color="Red (633nm)" package="5 mm [THT]"]
  LED4 = LED - 5mm [color="Red (633nm)" package="5 mm [THT]"]
  K2 = Relay [part_number=FRS1B-S package=THT]
  LED6 = LED - 5mm [color="Red (633nm)" package="5 mm [THT]"]
  S7 = SWITCH-DPDT [package=gpi-152-3013]
  LED7 = LED - 5mm [color="Red (633nm)" package="5 mm [THT]"]
  J1 = female pin header, 8 pins [form="♀ (female)"]

nets:
  GND: LED2.cathode, S1.L2, S2.L2, S3.L2, S4.COM, K1.COIL1, LED4.cathode, K2.COIL1, LED6.anode, S7.2, S7.5, J1.pin8
  N1: LED2.anode, K1.A, LED6.cathode
  N2: LED3.cathode, S4.L1
  N3: LED3.anode, K2.B, J1.pin1
  N4: S1.COM, J1.pin7
  N5: S2.COM, J1.pin6
  N6: S3.COM, J1.pin5
  N7: S4.L2, J1.pin4
  N8: K1.C2, K2.C1, K2.C2
  N9: K1.COIL2, K2.A, K2.COIL2, J1.pin2
  N10: K1.B, LED4.anode
  N11: LED5.cathode, S7.1
  N12: LED5.anode, LED7.anode
  N13: S7.3, LED7.cathode
  N14: S7.6, J1.pin3
