# Fritzing sketch InputStage (saved by Fritzing 0.9.3b)

parts:
  U4 = 941H-2C-5D [package=relay-5v]
  Master_Input = Stereo Jack (TRS) 3.5mm [package="PG203J [THT]"]
  ToMesaInput = Stereo Jack (TRS) 3.5mm [package="PG203J [THT]"]
  U5 = LM 358 Dual Op-Amp [package="DIP8 [THT]"]
  U6 = 941H-2C-5D [package=relay-5v]
  ToOrangeInput = Stereo Jack (TRS) 3.5mm [package="PG203J [THT]"]
  ToPihranaInput = Stereo Jack (TRS) 3.5mm [package="PG203J [THT]"]
  OrangeOut = Stereo Jack (TRS) 3.5mm [package="PG203J [THT]"]
  PihranaOut = Stereo Jack (TRS) 3.5mm [package="PG203J [THT]"]
  MesaOut = Stereo Jack (TRS) 3.5mm [package="PG203J [THT]"]
  R1 = Rotary Potentiometer (Large) [maximum_resistance=100kΩ package=THT]
  R2 = Rotary Potentiometer (Large) [maximum_resistance=100kΩ package=THT]
  ToEffects = Stereo Jack (TRS) 3.5mm [package="PG203J [THT]"]
  U7 = LM 358 Dual Op-Amp [package="DIP8 [THT]"]
  R3 = Resistor [tolerance=±5% resistance=220 package=THT]
  R4 = Resistor [tolerance=±5% resistance=220 package=THT]
  Effects_Return = Stereo Jack (TRS) 3.5mm [package="PG203J [THT]"]
  U8 = 941H-2C-5D [package=relay-5v]
  U9 = 941H-2C-5D [package=relay-5v]
  U10 = LM 358 Dual Op-Amp [package="DIP8 [THT]"]
  Effects_Return_2 = Stereo Jack (TRS) 3.5mm [package="PG203J [THT]"]
  R5 = Resistor [tolerance=±5% resistance=220 package=THT]
  R6 = Resistor [tolerance=±5% resistance=220 package=THT]
  J1 = female pin header, 4 pins [form="♀ (female)"]  # not connected

nets:
  N1: U4.4, U4.13, Master_Input.Ring
  N2: U4.8, U5.connector2, U5.connector4
  N3: U4.9, U5.connector5, U5.connector6
  N4: U4.11, ToMesaInput.Ring
  N5: U5.connector0, U5.connector1, U6.8
  -9V: U5.connector3, U7.connector3, U10.connector3
  9V: U5.connector7, U7.connector7, U10.connector7
  N6: U6.4, ToOrangeInput.Ring
  N7: U6.6, ToPihranaInput.Ring
  N8: U6.9, R2.leg2
  N9: U6.11, PihranaOut.Ring
  N10: U6.13, OrangeOut.Ring
  N11: MesaOut.Ring, R1.leg1
  N12: R1.wiper, U7.connector4
  GND: R1.leg2, R2.leg1, U8.16, U9.1
  N13: R2.wiper, U7.connector2
  N14: ToEffects.Ring, U8.9, U9.8
  N15: U7.connector0, U7.connector1, R3.Pin_1
  N16: U7.connector5, U7.connector6, R4.Pin_1
  N17: R3.Pin_0, U8.13
  N18: R4.Pin_0, U9.4
  N19: Effects_Return.Ring, U10.connector2
  N20: U8.11, U9.6, U10.connector4
  N21: U10.connector0, U10.connector1, R5.Pin_0
  N22: U10.connector5, U10.connector6, R6.Pin_1
  N23: Effects_Return_2.Ring, R5.Pin_1, R6.Pin_0

custom parts:
  941H-2C-5D: DPDT Relay - 2 Form C
