# Fritzing sketch PowerSwitchesWeek2 (saved by Fritzing 0.9.3b)
stripboards: 2

parts:
  ORANGE_LED = LED - 5mm [color="Red (633nm)" package="5 mm [THT]"]
  PIHRANA_LED = LED - 5mm [color="Red (635nm)" package="5 mm [THT]"]
  R7 = Resistor [tolerance=±10% resistance=390 package=THT]
  U7 = RELAY-2 [package=relay-g5v]
  R8 = Resistor [tolerance=±5% resistance=180 package=THT]
  J1 = female pin header, 2 pins [form="♀ (female)"]
  J2 = female pin header, 2 pins [form="♀ (female)"]
  LED1 = RGB LED (com. cathode, rgb) [package="5 mm [THT]"]
  J3 = female pin header, 2 pins [form="♀ (female)"]
  J5 = female pin header, 2 pins [form="♀ (female)"]
  J7 = female pin header, 2 pins [form="♀ (female)"]
  J8 = female pin header, 2 pins [form="♀ (female)"]
  J9 = female pin header, 2 pins [form="♀ (female)"]
  J10 = female pin header, 2 pins [form="♀ (female)"]
  J11 = female pin header, 2 pins [form="♀ (female)"]
  R6 = Resistor [tolerance=±5% resistance=1.2k package=THT]
  J4 = female pin header, 4 pins [form="♀ (female)"]
  D1 = Rectifier Diode [part_number=1N4001 package="300 mil [THT]"]
  D2 = Rectifier Diode [part_number=1N4001 package="300 mil [THT]"]
  D3 = Rectifier Diode [part_number=1N4001 package="300 mil [THT]"]
  D4 = Rectifier Diode [part_number=1N4001 package="300 mil [THT]"]
  R9 = Resistor [tolerance=±10% resistance=120 package=THT]
  R10 = Resistor [tolerance=±5% resistance=680 package=THT]
  Phirana_Switch = SWITCH-SPST-2 [package=switch-spst-vertical]
  Orange_Switch = SWITCH-SPST-2 [package=switch-spst-vertical]
  J12 = male pin header, 2 pins [form="♂ (male)"]
  9V = Power Jack [package=power_jack_combo]
  30V = Power Jack [package=power_jack_combo]
  15V = Power Jack [package=power_jack_combo]
  J13 = male pin header, 2 pins [form="♂ (male)"]
  J14 = male pin header, 2 pins [form="♂ (male)"]
  Main_Switch = SWITCH-SPST-2 [package=switch-spst-vertical]
  12V = Power Jack [package=power_jack_combo]

nets:
  GND: ORANGE_LED.cathode, PIHRANA_LED.cathode, J1.pin2, J2.pin2, LED1.common_cathode, J3.pin2, J8.pin2, J9.pin2, J10.pin2, J11.pin2, J4.pin2
  N1: ORANGE_LED.anode, J11.pin1, R9.Pin_1
  N2: PIHRANA_LED.anode, J10.pin1, R10.Pin_1
  N3: R7.Pin_0, R9.Pin_0
  N4: R7.Pin_1, J8.pin1, D1.cathode
  N5: U7.2, R8.Pin_0
  N6: U7.5, J3.pin1
  N7: U7.9, LED1.red_anode, J4.pin1
  N8: U7.10, D3.cathode
  N9: R8.Pin_1, J1.pin1, D4.cathode
  9V: J2.pin1, D3.anode
  N10: LED1.blue_anode, J4.pin4
  12V: J5.pin2, D4.anode
  N11: J7.pin1, D2.anode
  N12: J7.pin2, D1.anode
  N13: J9.pin1, R6.Pin_1, D2.cathode
  N14: R6.Pin_0, R10.Pin_0
  N15: Phirana_Switch.O, J12.pin1
  N16: Phirana_Switch.P, 30V.PWR
  N17: Orange_Switch.O, J12.pin2
  N18: Orange_Switch.P, 15V.PWR
  N19: 9V.GND, 9V.GNDBREAK, J13.pin1
  GND_2: 9V.PWR, 30V.GND, 30V.GNDBREAK, 15V.GND, 15V.GNDBREAK, J13.pin2, 12V.GND, 12V.GNDBREAK
  N20: J14.pin1, Main_Switch.O
  N21: Main_Switch.P, 12V.PWR
