# Fritzing sketch SignalManager2 (saved by Fritzing 0.9.3b)
stripboards: 1

parts:
  U4 = 941H-2C-5D [package=relay-5v]
  U5 = LM 358 Dual Op-Amp [package="DIP8 [THT]"]
  U7 = LM 358 Dual Op-Amp [package="DIP8 [THT]"]
  R4 = Resistor [tolerance=±5% resistance=1k package=THT]
  Effects_Return = Audio Jack (TRS) 3.5mm [package="4Ucon 08780 [THT]"]
  ToMesaInput = Audio Jack (TRS) 3.5mm [package="4Ucon 08780 [THT]"]
  ToOrangeInput = Audio Jack (TRS) 3.5mm [package="4Ucon 08780 [THT]"]
  ToPihranaInput = Audio Jack (TRS) 3.5mm [package="4Ucon 08780 [THT]"]
  Effects_Return_2 = Audio Jack (TRS) 3.5mm [package="4Ucon 08780 [THT]"]
  Master_Input = Audio Jack (TRS) 3.5mm [package="4Ucon 08780 [THT]"]
  OrangeOut = Audio Jack (TRS) 3.5mm [package="4Ucon 08780 [THT]"]
  PihranaOut = Audio Jack (TRS) 3.5mm [package="4Ucon 08780 [THT]"]
  ToEffects = Audio Jack (TRS) 3.5mm [package="4Ucon 08780 [THT]"]
  MesaOut = Audio Jack (TRS) 3.5mm [package="4Ucon 08780 [THT]"]
  J3 = female pin header, 2 pins [form="♀ (female)"]
  R8 = Resistor [tolerance=±5% resistance=100 package=THT]
  R9 = Resistor [tolerance=±5% resistance=100 package=THT]
  R11 = Resistor [tolerance=±5% resistance=1k package=THT]
  R13 = Resistor [tolerance=±5% resistance=47k package=THT]
  J5 = female pin header, 2 pins [form="♀ (female)"]
  ToOrangeInput_2 = male pin header, 2 pins [form="♂ (male)"]
  J9 = female pin header, 2 pins [form="♀ (female)"]
  PihranaOut_2 = male pin header, 2 pins [form="♂ (male)"]
  ToPihranaInput_2 = male pin header, 2 pins [form="♂ (male)"]
  J7 = female pin header, 2 pins [form="♀ (female)"]
  J11 = female pin header, 2 pins [form="♀ (female)"]
  OrangeOut_2 = male pin header, 2 pins [form="♂ (male)"]
  J13 = female pin header, 2 pins [form="♀ (female)"]
  MesaOut_2 = male pin header, 2 pins [form="♂ (male)"]
  J15 = female pin header, 2 pins [form="♀ (female)"]
  J17 = female pin header, 2 pins [form="♀ (female)"]
  Out = male pin header, 2 pins [form="♂ (male)"]
  J19 = female pin header, 2 pins [form="♀ (female)"]
  ToEffects_2 = male pin header, 2 pins [form="♂ (male)"]
  J21 = female pin header, 2 pins [form="♀ (female)"]
  AutoEffectsReturn = male pin header, 2 pins [form="♂ (male)"]
  R2 = Rotary Potentiometer (Large) [maximum_resistance=10kΩ package=THT]
  J2 = male pin header, 3 pins [form="♂ (male)"]
  J28 = male pin header, 5 pins [form="♂ (male)"]
  R12 = Resistor [tolerance=±5% resistance=47k package=THT]
  R10 = Resistor [tolerance=±5% resistance=1k package=THT]
  ToMesaInput_2 = male pin header, 2 pins [form="♂ (male)"]
  J30 = male pin header, 3 pins [form="♂ (male)"]
  J29 = female pin header, 3 pins [form="♀ (female)"]
  U6 = 941H-2C-5D [package=relay-5v]
  J31 = male pin header, 5 pins [form="♂ (male)"]
  U13 = RELAY-2 [package=relay-g5v]
  U12 = RELAY-2 [package=relay-g5v]
  R3 = Resistor [tolerance=±5% resistance=1k package=THT]
  J1 = female pin header, 5 pins [form="♀ (female)"]
  R14 = Resistor [tolerance=±5% resistance=1M package=THT]
  R15 = Resistor [tolerance=±5% resistance=1M package=THT]
  R16 = Resistor [tolerance=±5% resistance=1k package=THT]
  U11 = LM 358 Dual Op-Amp [package="DIP8 [THT]"]
  Master_Input_2 = male pin header, 2 pins [form="♂ (male)"]

nets:
  GND: U4.1, R8.Pin_1, R9.Pin_1, ToOrangeInput_2.pin2, PihranaOut_2.pin2, ToPihranaInput_2.pin2, OrangeOut_2.pin2, MesaOut_2.pin2, Out.pin2, ToEffects_2.pin2, AutoEffectsReturn.pin2, J2.pin1, J28.pin1, ToMesaInput_2.pin2, J29.pin2, U6.1, J31.pin1, U13.9, U12.9, R14.Pin_0, R15.Pin_1, Master_Input_2.pin2
  N1: U4.4, Out.pin1
  N2: U4.6, MesaOut_2.pin1, R15.Pin_0, U11.connector4
  N3: U4.8, U13.10, U12.10, R16.Pin_0
  N4: U4.11, U4.13, U5.connector2, ToMesaInput_2.pin1, Master_Input_2.pin1
  N5: U4.16, J1.pin4
  N6: U5.connector0, U5.connector1, U6.4
  -9V: U5.connector3, U7.connector3, J2.pin2, J28.pin2, J31.pin2, U11.connector3
  9V: U5.connector7, U7.connector7, J2.pin3, J28.pin4, J31.pin4, U11.connector7
  N7: U7.connector0, R10.Pin_0, R3.Pin_1
  N8: U7.connector1, R8.Pin_0, R10.Pin_1
  N9: U7.connector2, R12.Pin_0, J29.pin1
  N10: U7.connector4, R13.Pin_0, J29.pin3
  N11: U7.connector5, R9.Pin_0, R11.Pin_1
  N12: U7.connector6, R4.Pin_1, R11.Pin_0
  N13: R4.Pin_0, U13.6
  N14: Effects_Return.Sleeve, J17.pin2
  N15: Effects_Return.Ring, J17.pin1
  N16: ToMesaInput.Sleeve, J3.pin2
  N17: ToMesaInput.Ring, J3.pin1
  N18: ToOrangeInput.Sleeve, J5.pin2
  N19: ToOrangeInput.Ring, J5.pin1
  N20: ToPihranaInput.Sleeve, J7.pin2
  N21: ToPihranaInput.Ring, J7.pin1
  N22: Effects_Return_2.Sleeve, J21.pin2
  N23: Effects_Return_2.Ring, J21.pin1
  N24: Master_Input.Sleeve, J15.pin2
  N25: Master_Input.Ring, J15.pin1
  N26: OrangeOut.Sleeve, J11.pin2
  N27: OrangeOut.Ring, J11.pin1
  N28: PihranaOut.Sleeve, J9.pin2
  N29: PihranaOut.Ring, J9.pin1
  N30: ToEffects.Sleeve, J19.pin2
  N31: ToEffects.Ring, J19.pin1
  N32: MesaOut.Sleeve, J13.pin2
  N33: MesaOut.Ring, J13.pin1
  N34: R13.Pin_1, U11.connector5, U11.connector6
  N35: ToOrangeInput_2.pin1, U6.8
  N36: PihranaOut_2.pin1, U6.11
  N37: ToPihranaInput_2.pin1, U6.6
  N38: OrangeOut_2.pin1, U6.9
  N39: ToEffects_2.pin1, U13.1, U12.1
  N40: AutoEffectsReturn.pin1, R16.Pin_1
  N41: R2.leg1, J30.pin3
  N42: R2.wiper, J30.pin2
  N43: R2.leg2, J30.pin1
  N44: R12.Pin_1, U11.connector0, U11.connector1
  N45: U6.13, U11.connector2
  N46: U6.16, J1.pin3, R14.Pin_1
  N47: U13.2, J1.pin2
  N48: U12.2, J1.pin1
  N49: U12.5, R3.Pin_0

custom parts:
  941H-2C-5D: DPDT Relay - 2 Form C
