# Fritzing sketch SignalManagerWeek1 (saved by Fritzing 0.9.3b)
stripboards: 1

parts:
  U4 = 941H-2C-5D [package=relay-5v]
  U5 = LM 358 Dual Op-Amp [package="DIP8 [THT]"]
  U7 = LM 358 Dual Op-Amp [package="DIP8 [THT]"]
  R4 = Resistor [tolerance=±5% resistance=1k package=THT]
  Mesa_out = Audio Jack (TRS) 3.5mm [package="4Ucon 08780 [THT]"]
  ToMesaInput = Audio Jack (TRS) 3.5mm [package="4Ucon 08780 [THT]"]
  ToOrangeInput = Audio Jack (TRS) 3.5mm [package="4Ucon 08780 [THT]"]
  ToPihranaInput = Audio Jack (TRS) 3.5mm [package="4Ucon 08780 [THT]"]
  Effects_Return = Audio Jack (TRS) 3.5mm [package="4Ucon 08780 [THT]"]
  Master_Input = Audio Jack (TRS) 3.5mm [package="4Ucon 08780 [THT]"]
  OrangeOut = Audio Jack (TRS) 3.5mm [package="4Ucon 08780 [THT]"]
  PihranaOut = Audio Jack (TRS) 3.5mm [package="4Ucon 08780 [THT]"]
  ToEffects = Audio Jack (TRS) 3.5mm [package="4Ucon 08780 [THT]"]
  Mesa_In = Audio Jack (TRS) 3.5mm [package="4Ucon 08780 [THT]"]
  J3 = female pin header, 2 pins [form="♀ (female)"]
  R8 = Resistor [tolerance=±5% resistance=100 package=THT]
  R9 = Resistor [tolerance=±5% resistance=100 package=THT]
  R11 = Resistor [tolerance=±5% resistance=1k package=THT]
  R13 = Resistor [tolerance=±5% resistance=47k package=THT]
  J5 = female pin header, 2 pins [form="♀ (female)"]
  ToOrangeInput_2 = male pin header, 2 pins [form="♂ (male)"]
  J9 = female pin header, 2 pins [form="♀ (female)"]
  PihranaOut_2 = male pin header, 2 pins [form="♂ (male)"]
  ToPihranaInput_2 = male pin header, 2 pins [form="♂ (male)"]
  J7 = female pin header, 2 pins [form="♀ (female)"]
  J11 = female pin header, 2 pins [form="♀ (female)"]
  OrangeOut_2 = male pin header, 2 pins [form="♂ (male)"]
  J13 = female pin header, 2 pins [form="♀ (female)"]
  MesaIn = male pin header, 2 pins [form="♂ (male)"]
  J15 = female pin header, 2 pins [form="♀ (female)"]
  J17 = female pin header, 2 pins [form="♀ (female)"]
  Out = male pin header, 2 pins [form="♂ (male)"]
  J19 = female pin header, 2 pins [form="♀ (female)"]
  J21 = female pin header, 2 pins [form="♀ (female)"]
  AutoEffectsReturn = male pin header, 2 pins [form="♂ (male)"]
  R2 = Rotary Potentiometer (Large) [maximum_resistance=10kΩ package=THT]
  J2 = male pin header, 3 pins [form="♂ (male)"]
  J28 = male pin header, 5 pins [form="♂ (male)"]
  R12 = Resistor [tolerance=±5% resistance=47k package=THT]
  R10 = Resistor [tolerance=±5% resistance=1k package=THT]
  ToMesaInput_2 = male pin header, 2 pins [form="♂ (male)"]
  J30 = male pin header, 3 pins [form="♂ (male)"]
  J29 = female pin header, 3 pins [form="♀ (female)"]
  U6 = 941H-2C-5D [package=relay-5v]
  J31 = male pin header, 5 pins [form="♂ (male)"]
  U13 = RELAY-2 [package=relay-g5v]
  R3 = Resistor [tolerance=±5% resistance=1k package=THT]
  J1 = female pin header, 5 pins [form="♀ (female)"]
  R14 = Resistor [tolerance=±5% resistance=1M package=THT]
  R16 = Resistor [tolerance=±5% resistance=1k package=THT]
  U11 = LM 358 Dual Op-Amp [package="DIP8 [THT]"]
  Master_Input_2 = male pin header, 2 pins [form="♂ (male)"]
  C1 = Ceramic Capacitor [capacitance=100nF package="100 mil [THT, multilayer]"]
  C2 = Ceramic Capacitor [capacitance=100nF package="100 mil [THT, multilayer]"]
  C3 = Ceramic Capacitor [capacitance=100nF package="100 mil [THT, multilayer]"]
  R18 = Resistor [tolerance=±5% resistance=1M package=THT]
  R17 = Resistor [tolerance=±5% resistance=1M package=THT]
  U12 = RELAY-2 [package=relay-g5v]
  R19 = Resistor [tolerance=±5% resistance=1M package=THT]
  ToEffects_2 = male pin header, 2 pins [form="♂ (male)"]

nets:
  GND: U4.1, R8.Pin_1, R9.Pin_1, ToOrangeInput_2.pin2, PihranaOut_2.pin2, ToPihranaInput_2.pin2, OrangeOut_2.pin2, MesaIn.pin2, Out.pin2, AutoEffectsReturn.pin2, J2.pin1, J28.pin1, ToMesaInput_2.pin2, J29.pin2, U6.1, J31.pin1, U13.9, R14.Pin_0, Master_Input_2.pin2, R18.Pin_0, R17.Pin_0, U12.9, R19.Pin_1, ToEffects_2.pin2
  N1: U4.4, Out.pin1
  N2: U4.6, MesaIn.pin1, C2.0
  N3: U4.8, U13.10, R16.Pin_0, U12.10
  N4: U4.11, U4.13, ToMesaInput_2.pin1, Master_Input_2.pin1, C1.1
  N5: U4.16, J1.pin4
  N6: U5.connector0, U5.connector1, U6.4
  N7: U5.connector2, C1.0, R17.Pin_1
  -9V: U5.connector3, U7.connector3, J2.pin2, J28.pin2, J31.pin2, U11.connector3
  9V: U5.connector7, U7.connector7, J2.pin3, J28.pin4, J31.pin4, U11.connector7
  N8: U7.connector0, R10.Pin_0, R3.Pin_1
  N9: U7.connector1, R8.Pin_0, R10.Pin_1
  N10: U7.connector2, R12.Pin_0, J29.pin1
  N11: U7.connector4, R13.Pin_0, J29.pin3
  N12: U7.connector5, R9.Pin_0, R11.Pin_1
  N13: U7.connector6, R4.Pin_1, R11.Pin_0
  N14: R4.Pin_0, U13.6
  N15: Mesa_out.Sleeve, J17.pin2
  N16: Mesa_out.Ring, J17.pin1
  N17: ToMesaInput.Sleeve, J3.pin2
  N18: ToMesaInput.Ring, J3.pin1
  N19: ToOrangeInput.Sleeve, J5.pin2
  N20: ToOrangeInput.Ring, J5.pin1
  N21: ToPihranaInput.Sleeve, J7.pin2
  N22: ToPihranaInput.Ring, J7.pin1
  N23: Effects_Return.Sleeve, J21.pin2
  N24: Effects_Return.Ring, J21.pin1
  N25: Master_Input.Sleeve, J15.pin2
  N26: Master_Input.Ring, J15.pin1
  N27: OrangeOut.Sleeve, J11.pin2
  N28: OrangeOut.Ring, J11.pin1
  N29: PihranaOut.Sleeve, J9.pin2
  N30: PihranaOut.Ring, J9.pin1
  N31: ToEffects.Sleeve, J19.pin2
  N32: ToEffects.Ring, J19.pin1
  N33: Mesa_In.Sleeve, J13.pin2
  N34: Mesa_In.Ring, J13.pin1
  N35: R13.Pin_1, U11.connector5, U11.connector6
  N36: ToOrangeInput_2.pin1, U6.8
  N37: PihranaOut_2.pin1, U6.11
  N38: ToPihranaInput_2.pin1, U6.6
  N39: OrangeOut_2.pin1, U6.9
  N40: AutoEffectsReturn.pin1, R16.Pin_1
  N41: R2.leg1, J30.pin3
  N42: R2.wiper, J30.pin2
  N43: R2.leg2, J30.pin1
  N44: J28.pin3, J31.pin3
  N45: J28.pin5, J31.pin5
  N46: R12.Pin_1, U11.connector0, U11.connector1
  N47: U6.13, C3.1
  N48: U6.16, J1.pin3, R14.Pin_1
  N49: U13.1, U12.1, ToEffects_2.pin1
  N50: U13.2, J1.pin2
  N51: R3.Pin_0, U12.5
  N52: J1.pin1, U12.2
  N53: U11.connector2, C3.0
  N54: U11.connector4, C2.1, R19.Pin_0

custom parts:
  941H-2C-5D: DPDT Relay - 2 Form C
