# Fritzing sketch Switching (saved by Fritzing 0.9.3b)
stripboards: 2

parts:
  Q1 = NPN-Transistor [package="TO92 [THT]"]
  Q3 = NPN-Transistor [package="TO92 [THT]"]
  J3 = male pin header, 2 pins [form="♂ (male)"]
  J1 = male pin header, 2 pins [form="♂ (male)"]
  J2 = male pin header, 2 pins [form="♂ (male)"]
  J4 = male pin header, 3 pins [form="♂ (male)"]
  Q2 = NPN-Transistor [package="TO92 [THT]"]
  J5 = male pin header, 3 pins [form="♂ (male)"]
  J6 = male pin header, 3 pins [form="♂ (male)"]
  J7 = male pin header, 3 pins [form="♂ (male)"]
  J8 = female pin header, 3 pins [form="♀ (female)"]
  J9 = male pin header, 5 pins [form="♂ (male)"]
  J10 = male pin header, 3 pins [form="♂ (male)"]
  J13 = female pin header, 3 pins [form="♀ (female)"]
  J14 = male pin header, 5 pins [form="♂ (male)"]
  IC5 = L293D [package=THT]
  IC6 = L293D [package=THT]
  BlendMotorOut = female pin header, 2 pins [form="♀ (female)"]
  ToneMotorOut = female pin header, 2 pins [form="♀ (female)"]
  GainMotorOut = female pin header, 2 pins [form="♀ (female)"]
  VolumeMotorOut = female pin header, 2 pins [form="♀ (female)"]
  MotorControlPins = female pin header, 8 pins [form="♀ (female)"]  # not connected
  J11 = male pin header, 3 pins [form="♂ (male)"]
  J51 = male pin header, 3 pins [form="♂ (male)"]
  1k = Resistor [tolerance=±5% resistance=10k package=THT]
  R3 = Resistor [tolerance=±5% resistance=10k package=THT]
  R2 = Resistor [tolerance=±5% resistance=10k package=THT]
  J58 = female pin header, 2 pins [form="♀ (female)"]
  J59 = female pin header, 2 pins [form="♀ (female)"]
  IC7 = Dual Op-Amp [package=dip08]
  R15 = Rotary Potentiometer (Large) [maximum_resistance=10kΩ package=THT]
  R16 = Resistor [tolerance=±5% resistance=4.7k package=THT]
  R17 = Resistor [tolerance=±10% resistance=4.7k package=THT]
  J60 = female pin header, 4 pins [form="♀ (female)"]
  IC8 = IC, DIP package, 8 pins [chip_label=IC]
  IC9 = IC, DIP package, 8 pins [chip_label=IC]
  C8 = Electrolytic Capacitor [capacitance=1µF package="100 mil [THT, electrolytic]"]
  C9 = Electrolytic Capacitor [capacitance=1µF package="100 mil [THT, electrolytic]"]
  C10 = Electrolytic Capacitor [capacitance=1µF package="100 mil [THT, electrolytic]"]
  IC10 = IC, DIP package, 8 pins [chip_label=IC]
  C11 = Electrolytic Capacitor [capacitance=1µF package="100 mil [THT, electrolytic]"]
  J61 = female pin header, 2 pins [form="♀ (female)"]
  R18 = Resistor [tolerance=±5% resistance=10k package=THT]
  R19 = Resistor [tolerance=±5% resistance=12k package=THT]
  Q4 = NPN-Transistor [package="TO92 [THT]"]
  R20 = Resistor [tolerance=±5% resistance=10k package=THT]
  J62 = male pin header, 2 pins [form="♂ (male)"]
  Q5 = Basic FET N-Channel [package="TO220 [THT]"]
  R21 = Resistor [tolerance=±5% resistance=10k package=THT]

nets:
  GND: Q1.E, Q3.E, J3.pin2, J1.pin2, J2.pin2, Q2.E, J5.pin1, J6.pin1, J7.pin1, J9.pin5, J10.pin1, J14.pin5, IC5.0V, IC6.0V, J11.pin1, J51.pin1, J58.pin2, IC7.A_V-, R16.Pin_1, IC8.pin3, IC9.pin3, C8.+, IC10.pin3, J61.pin2, R19.Pin_1, Q4.E, J62.pin2
  N1: Q1.B, 1k.Pin_1
  N2: Q1.C, J2.pin1
  N3: Q3.B, R3.Pin_1
  N4: Q3.C, J1.pin1
  N5: J3.pin1, Q2.C
  N6: J4.pin1, 1k.Pin_0
  N7: J4.pin2, R2.Pin_0
  N8: J4.pin3, R3.Pin_0
  N9: Q2.B, R2.Pin_1
  7V: J5.pin2, J6.pin2, J7.pin2, J10.pin2, J11.pin2, J51.pin2, IC7.B_-IN, IC7.B_OUT
  N10: J5.pin3, J8.pin1
  N11: J6.pin3, J8.pin2
  N12: J7.pin3, J8.pin3
  5V: J9.pin1, J14.pin1, IC5.Enable_1, IC5.Enable_2, IC5.+V, IC6.Enable_1, IC6.Enable_2, IC6.+V
  9V: J9.pin2, J14.pin2, R17.Pin_0, IC8.pin1, IC8.pin8, IC9.pin1, IC9.pin8, IC10.pin1, IC10.pin8, J61.pin1, R21.Pin_0
  -9V: J9.pin4, J14.pin4, IC8.pin5, IC9.pin5, C8.-, IC10.pin5
  N13: J10.pin3, J13.pin3
  N14: J13.pin1, J51.pin3
  N15: J13.pin2, J11.pin3
  N16: IC5.Out_1_(_Controlled_by_Enable_1_), ToneMotorOut.pin1
  N17: IC5.Out_2_(_Controlled_by_Enable_1_), ToneMotorOut.pin2
  12V: IC5.+Vmotor, IC6.+Vmotor, IC7.A_V+, R18.Pin_0, Q5.drain
  N18: IC5.Out_3_(_Controlled_by_Enable_2_), VolumeMotorOut.pin2
  N19: IC5.Out_4_(_Controlled_by_Enable_2_), VolumeMotorOut.pin1
  N20: IC6.Out_1_(_Controlled_by_Enable_1_), BlendMotorOut.pin1
  N21: IC6.Out_2_(_Controlled_by_Enable_1_), BlendMotorOut.pin2
  N22: IC6.Out_3_(_Controlled_by_Enable_2_), GainMotorOut.pin2
  N23: IC6.Out_4_(_Controlled_by_Enable_2_), GainMotorOut.pin1
  N24: J58.pin1, Q5.source
  N25: J59.pin1, J60.pin4
  N26: J59.pin2, J60.pin1
  N27: IC7.A_OUT, IC7.A_-IN
  N28: IC7.A_+IN, R15.wiper
  N29: IC7.B_+IN, R18.Pin_1, R19.Pin_0
  N30: R15.leg1, R17.Pin_1
  N31: R15.leg2, R16.Pin_0
  N32: IC8.pin2, C9.+
  N33: IC8.pin4, C9.-
  N34: IC9.pin2, C10.+
  N35: IC9.pin4, C10.-
  N36: IC10.pin2, C11.+
  N37: IC10.pin4, C11.-
  N38: Q4.B, R20.Pin_1
  N39: Q4.C, J62.pin1
  N40: Q5.gate, R21.Pin_1
