# Fritzing sketch Switching3 (saved by Fritzing 0.9.3b)
stripboards: 2

parts:
  Q1 = NPN-Transistor [package="TO92 [THT]"]
  Q3 = NPN-Transistor [package="TO92 [THT]"]
  J3 = male pin header, 2 pins [form="♂ (male)"]
  J1 = male pin header, 2 pins [form="♂ (male)"]
  J2 = male pin header, 2 pins [form="♂ (male)"]
  Q2 = NPN-Transistor [package="TO92 [THT]"]
  J5 = male pin header, 3 pins [form="♂ (male)"]
  J6 = male pin header, 3 pins [form="♂ (male)"]
  J7 = male pin header, 3 pins [form="♂ (male)"]
  J8 = female pin header, 3 pins [form="♀ (female)"]
  J9 = male pin header, 5 pins [form="♂ (male)"]
  J10 = male pin header, 3 pins [form="♂ (male)"]
  J13 = female pin header, 3 pins [form="♀ (female)"]
  J14 = male pin header, 5 pins [form="♂ (male)"]  # not connected
  IC5 = L293D [package=THT]
  IC6 = L293D [package=THT]
  BlendMotorOut = female pin header, 2 pins [form="♀ (female)"]
  ToneMotorOut = female pin header, 2 pins [form="♀ (female)"]
  GainMotorOut = female pin header, 2 pins [form="♀ (female)"]
  VolumeMotorOut = female pin header, 2 pins [form="♀ (female)"]
  MotorControlPins = female pin header, 8 pins [form="♀ (female)"]  # not connected
  J11 = male pin header, 3 pins [form="♂ (male)"]
  J51 = male pin header, 3 pins [form="♂ (male)"]
  1k = Resistor [tolerance=±5% resistance=10k package=THT]
  R3 = Resistor [tolerance=±5% resistance=10k package=THT]
  R2 = Resistor [tolerance=±5% resistance=10k package=THT]
  IC7 = Dual Op-Amp [package=dip08]
  R15 = Rotary Potentiometer (Large) [maximum_resistance=10kΩ package=THT]
  R16 = Resistor [tolerance=±5% resistance=4.7k package=THT]
  R17 = Resistor [tolerance=±10% resistance=4.7k package=THT]
  IC8 = IC, DIP package, 8 pins [chip_label=IC]
  IC9 = IC, DIP package, 8 pins [chip_label=IC]
  C8 = Electrolytic Capacitor [capacitance=1µF package="100 mil [THT, electrolytic]"]
  C9 = Electrolytic Capacitor [capacitance=1µF package="100 mil [THT, electrolytic]"]
  C10 = Electrolytic Capacitor [capacitance=1µF package="100 mil [THT, electrolytic]"]
  C11 = Electrolytic Capacitor [capacitance=1µF package="100 mil [THT, electrolytic]"]
  R18 = Resistor [tolerance=±5% resistance=10k package=THT]
  R19 = Resistor [tolerance=±5% resistance=12k package=THT]
  Q4 = NPN-Transistor [package="TO92 [THT]"]
  R20 = Resistor [tolerance=±5% resistance=10k package=THT]
  J62 = male pin header, 2 pins [form="♂ (male)"]
  J58 = female pin header, 2 pins [form="♀ (female)"]
  J61 = female pin header, 2 pins [form="♀ (female)"]
  J4 = male pin header, 4 pins [form="♂ (male)"]
  IC11 = IC, DIP package, 8 pins [chip_label=IC]
  Q6 = PNP-Transistor [package="TO92 [THT]"]
  R23 = Resistor [tolerance=±5% resistance=15k package=THT]
  R21 = Resistor [tolerance=±5% resistance=10k package=THT]
  R22 = Resistor [tolerance=±5% resistance=220 package=THT]
  Q7 = PNP-Transistor [package="TO92 [THT]"]
  R24 = Resistor [tolerance=±5% resistance=10k package=THT]
  R25 = Resistor [tolerance=±5% resistance=220 package=THT]
  R26 = Resistor [tolerance=±5% resistance=15k package=THT]
  Q8 = PNP-Transistor [package="TO92 [THT]"]
  Q9 = PNP-Transistor [package="TO92 [THT]"]
  R27 = Resistor [tolerance=±5% resistance=10k package=THT]
  R28 = Resistor [tolerance=±5% resistance=10k package=THT]
  R29 = Resistor [tolerance=±5% resistance=220 package=THT]
  R30 = Resistor [tolerance=±5% resistance=220 package=THT]
  R31 = Resistor [tolerance=±5% resistance=15k package=THT]
  R32 = Resistor [tolerance=±5% resistance=15k package=THT]
  Q10 = PNP-Transistor [package="TO92 [THT]"]
  R33 = Resistor [tolerance=±5% resistance=220 package=THT]
  R34 = Resistor [tolerance=±5% resistance=10k package=THT]
  R35 = Resistor [tolerance=±5% resistance=15k package=THT]
  J64 = female pin header, 9 pins [form="♀ (female)"]
  J65 = male pin header, 5 pins [form="♂ (male)"]
  J66 = male pin header, 5 pins [form="♂ (male)"]
  R36 = Resistor [tolerance=±5% resistance=220k package=THT]
  R37 = Resistor [tolerance=±5% resistance=220k package=THT]
  R38 = Resistor [tolerance=±5% resistance=220k package=THT]
  R39 = Resistor [tolerance=±5% resistance=220k package=THT]
  J63 = female alternating pin header, 6 pins [form="♀ (female)"]

nets:
  GND: Q1.E, Q3.E, J3.pin2, J1.pin2, J2.pin2, Q2.E, J5.pin1, J6.pin1, J7.pin1, J9.pin5, J10.pin1, IC5.0V, IC6.0V, J11.pin1, J51.pin1, IC7.A_V-, R16.Pin_1, IC8.pin3, IC9.pin3, C8.+, R19.Pin_1, Q4.E, J62.pin2, J58.pin2, J61.pin2, IC11.pin3
  N1: Q1.B, 1k.Pin_1
  N2: Q1.C, J2.pin1
  N3: Q3.B, R3.Pin_1
  N4: Q3.C, J1.pin1
  N5: J3.pin1, Q2.C
  N6: Q2.B, R2.Pin_1
  7V: J5.pin2, J6.pin2, J7.pin2, J10.pin2, J11.pin2, J51.pin2, IC7.B_-IN, IC7.B_OUT
  N7: J5.pin3, J8.pin1
  N8: J6.pin3, J8.pin2
  N9: J7.pin3, J8.pin3
  5V/9V: J9.pin1, J9.pin2, IC5.Enable_1, IC5.Enable_2, IC5.+V, IC6.Enable_1, IC6.Out_1_(_Controlled_by_Enable_1_), IC6.Enable_2, IC6.+V, BlendMotorOut.pin1, R17.Pin_0, IC8.pin1, IC8.pin8, IC9.pin1, IC9.pin8, J61.pin1, IC11.pin1, IC11.pin8
  -9V: J9.pin4, IC8.pin5, IC9.pin5, C8.-, IC11.pin5, IC11.pin6
  N10: J10.pin3, J13.pin3
  N11: J13.pin1, J51.pin3
  N12: J13.pin2, J11.pin3
  N13: IC5.In_1, IC6.Out_2_(_Controlled_by_Enable_1_), BlendMotorOut.pin2
  N14: IC5.Out_1_(_Controlled_by_Enable_1_), ToneMotorOut.pin1
  N15: IC5.Out_2_(_Controlled_by_Enable_1_), ToneMotorOut.pin2
  12V: IC5.+Vmotor, IC6.+Vmotor, IC7.A_V+, R18.Pin_0, J58.pin1
  N16: IC5.Out_3_(_Controlled_by_Enable_2_), VolumeMotorOut.pin2
  N17: IC5.Out_4_(_Controlled_by_Enable_2_), VolumeMotorOut.pin1
  N18: IC6.Out_3_(_Controlled_by_Enable_2_), GainMotorOut.pin2
  N19: IC6.Out_4_(_Controlled_by_Enable_2_), GainMotorOut.pin1
  N20: 1k.Pin_0, J4.pin1
  N21: R3.Pin_0, J4.pin3
  N22: R2.Pin_0, J4.pin2
  N23: IC7.A_OUT, IC7.A_-IN
  N24: IC7.A_+IN, R15.wiper
  N25: IC7.B_+IN, R18.Pin_1, R19.Pin_0
  N26: R15.leg1, R17.Pin_1
  N27: R15.leg2, R16.Pin_0
  N28: IC8.pin2, C9.+
  N29: IC8.pin4, C9.-
  N30: IC9.pin2, C10.+
  N31: IC9.pin4, C10.-
  N32: C11.-, IC11.pin4
  N33: C11.+, IC11.pin2
  N34: Q4.B, R20.Pin_1
  N35: Q4.C, J62.pin1
  N36: R20.Pin_0, J4.pin4
  N37: Q6.E, R21.Pin_0, Q7.E, R24.Pin_0, Q8.E, Q9.E, R27.Pin_0, R28.Pin_0, Q10.E, R34.Pin_0, J65.pin3, J66.pin3
  N38: Q6.B, R23.Pin_1, R21.Pin_1
  N39: Q6.C, R22.Pin_0
  N40: R23.Pin_0, J63.pin6
  N41: R22.Pin_1, J64.pin9
  N42: Q7.B, R24.Pin_1, R26.Pin_1
  N43: Q7.C, R25.Pin_0
  N44: R25.Pin_1, J64.pin8
  N45: R26.Pin_0, J63.pin5
  N46: Q8.B, R27.Pin_1, R31.Pin_1
  N47: Q8.C, R30.Pin_0
  N48: Q9.B, R28.Pin_1, R32.Pin_1
  N49: Q9.C, R29.Pin_0
  N50: R29.Pin_1, J64.pin6
  N51: R30.Pin_1, J64.pin7
  N52: R31.Pin_0, J63.pin4
  N53: R32.Pin_0, J63.pin3
  N54: Q10.B, R34.Pin_1, R35.Pin_1
  N55: Q10.C, R33.Pin_0
  N56: R35.Pin_0, J63.pin1
  N57: J64.pin5, J65.pin1, J66.pin1
  N58: J65.pin2, J66.pin2
  N59: J65.pin4, J66.pin4
  N60: J65.pin5, J66.pin5, R36.Pin_1, R37.Pin_1, R38.Pin_1, R39.Pin_1
