# Fritzing sketch SwitchingWeek2 (saved by Fritzing 0.9.3b)
stripboards: 2

parts:
  Q1 = NPN-Transistor [package="TO92 [THT]"]
  Q3 = NPN-Transistor [package="TO92 [THT]"]
  J3 = male pin header, 2 pins [form="♂ (male)"]
  J1 = male pin header, 2 pins [form="♂ (male)"]
  J2 = male pin header, 2 pins [form="♂ (male)"]
  Q2 = NPN-Transistor [package="TO92 [THT]"]
  J5 = male pin header, 3 pins [form="♂ (male)"]
  J6 = male pin header, 3 pins [form="♂ (male)"]
  J7 = male pin header, 3 pins [form="♂ (male)"]
  Oranger_Servo = female pin header, 3 pins [form="♀ (female)"]
  J10 = male pin header, 3 pins [form="♂ (male)"]
  Pihrana_Servo = female pin header, 3 pins [form="♀ (female)"]
  Power = male pin header, 5 pins [form="♂ (male)"]
  IC5 = L293D [package=THT]
  IC6 = L293D [package=THT]
  J11 = male pin header, 3 pins [form="♂ (male)"]
  J51 = male pin header, 3 pins [form="♂ (male)"]
  1k = Resistor [tolerance=±5% resistance=10k package=THT]
  R3 = Resistor [tolerance=±5% resistance=10k package=THT]
  R2 = Resistor [tolerance=±5% resistance=10k package=THT]
  IC7 = Dual Op-Amp [package=dip08]
  R15 = Rotary Potentiometer (Large) [maximum_resistance=10kΩ package=THT]
  R16 = Resistor [tolerance=±5% resistance=4.7k package=THT]
  R17 = Resistor [tolerance=±10% resistance=4.7k package=THT]
  IC8 = IC, DIP package, 8 pins [chip_label=IC]
  IC9 = IC, DIP package, 8 pins [chip_label=IC]
  C8 = Electrolytic Capacitor [capacitance=1µF package="100 mil [THT, electrolytic]"]
  C9 = Electrolytic Capacitor [capacitance=1µF package="100 mil [THT, electrolytic]"]
  C10 = Electrolytic Capacitor [capacitance=1µF package="100 mil [THT, electrolytic]"]
  C11 = Electrolytic Capacitor [capacitance=1µF package="100 mil [THT, electrolytic]"]
  R18 = Resistor [tolerance=±5% resistance=10k package=THT]
  R19 = Resistor [tolerance=±5% resistance=12k package=THT]
  Q4 = NPN-Transistor [package="TO92 [THT]"]
  R20 = Resistor [tolerance=±5% resistance=10k package=THT]
  J62 = male pin header, 2 pins [form="♂ (male)"]
  12_Volt_Power = female pin header, 2 pins [form="♀ (female)"]
  9V_Power_In = female pin header, 2 pins [form="♀ (female)"]
  J4 = male pin header, 4 pins [form="♂ (male)"]
  Q6 = PNP-Transistor [package="TO92 [THT]"]
  R23 = Resistor [tolerance=±5% resistance=15k package=THT]
  R21 = Resistor [tolerance=±5% resistance=10k package=THT]
  R22 = Resistor [tolerance=±5% resistance=220 package=THT]
  Q7 = PNP-Transistor [package="TO92 [THT]"]
  R24 = Resistor [tolerance=±5% resistance=10k package=THT]
  R25 = Resistor [tolerance=±5% resistance=220 package=THT]
  R26 = Resistor [tolerance=±5% resistance=15k package=THT]
  Q8 = PNP-Transistor [package="TO92 [THT]"]
  Q9 = PNP-Transistor [package="TO92 [THT]"]
  R27 = Resistor [tolerance=±5% resistance=10k package=THT]
  R28 = Resistor [tolerance=±5% resistance=10k package=THT]
  R29 = Resistor [tolerance=±5% resistance=220 package=THT]
  R30 = Resistor [tolerance=±5% resistance=220 package=THT]
  R31 = Resistor [tolerance=±5% resistance=15k package=THT]
  R32 = Resistor [tolerance=±5% resistance=15k package=THT]
  Q10 = PNP-Transistor [package="TO92 [THT]"]
  R33 = Resistor [tolerance=±5% resistance=220 package=THT]
  R34 = Resistor [tolerance=±5% resistance=10k package=THT]
  R35 = Resistor [tolerance=±5% resistance=15k package=THT]
  J64 = female pin header, 9 pins [form="♀ (female)"]
  J65 = male pin header, 5 pins [form="♂ (male)"]
  J66 = male pin header, 5 pins [form="♂ (male)"]
  R36 = Resistor [tolerance=±5% resistance=220k package=THT]
  R37 = Resistor [tolerance=±5% resistance=220k package=THT]
  R38 = Resistor [tolerance=±5% resistance=220k package=THT]
  R39 = Resistor [tolerance=±5% resistance=220k package=THT]
  J63 = female alternating pin header, 6 pins [form="♀ (female)"]
  12_Volt_Power_2 = female pin header, 2 pins [form="♀ (female)"]
  Motor3and4Out = female pin header, 10 pins [form="♀ (female)"]
  Motor1and2Out = female pin header, 10 pins [form="♀ (female)"]
  MotorPotsToArduino = female pin header, 4 pins [form="♀ (female)"]
  Motors1and2ControlPins1 = female pin header, 4 pins [form="♀ (female)"]
  Motors3and4ControlPins = female pin header, 4 pins [form="♀ (female)"]
  C12 = Electrolytic Capacitor [capacitance=10µF package="100 mil [THT, electrolytic]"]
  L7805ACV = Voltage Regulator - 5V [package="TO220 [THT]"]
  C13 = Electrolytic Capacitor [capacitance=10µF package="100 mil [THT, electrolytic]"]
  Power1 = male pin header, 5 pins [form="♂ (male)"]
  C14 = Electrolytic Capacitor [capacitance=1µF package="100 mil [THT, electrolytic]"]
  C15 = Electrolytic Capacitor [capacitance=1µF package="100 mil [THT, electrolytic]"]
  IC11 = IC, DIP package, 8 pins [chip_label=IC]
  SWITCHES = female pin header, 4 pins [form="♀ (female)"]
  L7805ACV1 = Voltage Regulator - 5V [package="TO220 [THT]"]
  R41 = Resistor [tolerance=±5% resistance=100 package=THT]
  R42 = Resistor [tolerance=±5% resistance=470 package=THT]
  C16 = Electrolytic Capacitor [capacitance=10µF package="100 mil [THT, electrolytic]"]

nets:
  GND: Q1.E, Q3.E, J3.pin2, J1.pin2, J2.pin2, Q2.E, J5.pin1, J6.pin1, J7.pin1, J10.pin1, Power.pin5, IC5.0V, IC6.0V, J11.pin1, J51.pin1, IC7.A_V-, R16.Pin_1, IC8.pin3, IC9.pin3, C8.+, R19.Pin_1, Q4.E, J62.pin2, 12_Volt_Power.pin2, 9V_Power_In.pin1, J65.pin5, J66.pin5, R36.Pin_1, R37.Pin_1, R38.Pin_1, R39.Pin_1, 12_Volt_Power_2.pin2, Motor3and4Out.pin5, Motor3and4Out.pin10, Motor1and2Out.pin1, Motor1and2Out.pin6, C12.-, L7805ACV.GND, C13.-, Power1.pin5, C14.+, C15.+, IC11.pin3, R41.Pin_1, C16.-
  N1: Q1.B, 1k.Pin_1
  N2: Q1.C, J2.pin1
  N3: Q3.B, R3.Pin_1
  N4: Q3.C, J1.pin1
  N5: J3.pin1, Q2.C
  N6: Q2.B, R2.Pin_1
  6V/7V: J5.pin2, J6.pin2, J7.pin2, J10.pin2, J11.pin2, J51.pin2, IC7.B_-IN, IC7.B_OUT, L7805ACV1.output_voltage, R42.Pin_1, C16.+
  OGain: J5.pin3, Oranger_Servo.pin1
  OTone: J6.pin3, Oranger_Servo.pin2
  OVol: J7.pin3, Oranger_Servo.pin3
  PVol: J10.pin3, Pihrana_Servo.pin3
  PGain: Pihrana_Servo.pin1, J51.pin3
  PTone: Pihrana_Servo.pin2, J11.pin3
  5V: Power.pin1, IC5.Enable_1, IC5.Enable_2, IC5.+V, IC6.Enable_1, IC6.Enable_2, IC6.+V, J64.pin5, J65.pin1, J66.pin1, Motor3and4Out.pin3, Motor3and4Out.pin8, Motor1and2Out.pin3, Motor1and2Out.pin8, L7805ACV.output_voltage, C13.+, Power1.pin1
  9V: Power.pin2, R17.Pin_0, IC8.pin1, IC8.pin8, IC9.pin1, IC9.pin8, 9V_Power_In.pin2, J65.pin2, J66.pin2, Power1.pin2, IC11.pin1, IC11.pin8
  LED Power: Power.pin3, IC7.A_OUT, IC7.A_-IN, Q6.E, R21.Pin_0, Q7.E, R24.Pin_0, Q8.E, Q9.E, R27.Pin_0, R28.Pin_0, Q10.E, R34.Pin_0, J65.pin3, J66.pin3, Power1.pin3
  -9V: Power.pin4, IC8.pin5, IC9.pin5, C8.-, J65.pin4, J66.pin4, Power1.pin4, C14.-, C15.-, IC11.pin5
  Motor2Input1: IC5.In_1, Motors1and2ControlPins1.pin1
  Motor2Out1: IC5.Out_1_(_Controlled_by_Enable_1_), Motor1and2Out.pin10
  Motor2Out2: IC5.Out_2_(_Controlled_by_Enable_1_), Motor1and2Out.pin9
  Motor2Input2: IC5.In_2, Motors1and2ControlPins1.pin2
  12V: IC5.+Vmotor, IC6.+Vmotor, IC7.A_V+, R18.Pin_0, 12_Volt_Power.pin1, 12_Volt_Power_2.pin1, C12.+, L7805ACV.input_voltage, L7805ACV1.input_voltage
  Motor4Input2: IC5.In_3, Motors3and4ControlPins.pin4
  Motor4Out2: IC5.Out_3_(_Controlled_by_Enable_2_), Motor3and4Out.pin7
  Motor4Out1: IC5.Out_4_(_Controlled_by_Enable_2_), Motor3and4Out.pin6
  Motor4Input1: IC5.In_4, Motors3and4ControlPins.pin3
  Motor1Input1: IC6.In_1, Motors1and2ControlPins1.pin3
  Motor1Out1: IC6.Out_1_(_Controlled_by_Enable_1_), Motor1and2Out.pin5
  Motor1Out2: IC6.Out_2_(_Controlled_by_Enable_1_), Motor1and2Out.pin4
  Motor1Input2: IC6.In_2, Motors1and2ControlPins1.pin4
  Motor3Input2: IC6.In_3, Motors3and4ControlPins.pin2
  Motor3Out2: IC6.Out_3_(_Controlled_by_Enable_2_), Motor3and4Out.pin2
  Motor3Out1: IC6.Out_4_(_Controlled_by_Enable_2_), Motor3and4Out.pin1
  Motor3Input1: IC6.In_4, Motors3and4ControlPins.pin1
  Ch2: 1k.Pin_0, J4.pin1
  Solo: R3.Pin_0, J4.pin3
  Ch3: R2.Pin_0, J4.pin2
  N7: IC7.A_+IN, R15.wiper
  N8: IC7.B_+IN, R18.Pin_1, R19.Pin_0
  N9: R15.leg1, R17.Pin_1
  N10: R15.leg2, R16.Pin_0
  N11: IC8.pin2, C9.+
  N12: IC8.pin4, C9.-
  N13: IC9.pin2, C10.+
  N14: IC9.pin4, C10.-
  N15: C11.-, IC11.pin4
  N16: C11.+, IC11.pin2
  N17: Q4.B, R20.Pin_1
  N18: Q4.C, J62.pin1
  OtherSwitch: R20.Pin_0, J4.pin4
  N19: Q6.B, R23.Pin_1, R21.Pin_1
  N20: Q6.C, R22.Pin_0
  LEDCNTRL1: R23.Pin_0, J63.pin6
  2LED1: R22.Pin_1, J64.pin9
  N21: Q7.B, R24.Pin_1, R26.Pin_1
  N22: Q7.C, R25.Pin_0
  2LED3: R25.Pin_1, J64.pin8
  LEDCNTRL3: R26.Pin_0, J63.pin5
  N23: Q8.B, R27.Pin_1, R31.Pin_1
  N24: Q8.C, R30.Pin_0
  N25: Q9.B, R28.Pin_1, R32.Pin_1
  N26: Q9.C, R29.Pin_0
  2LED4: R29.Pin_1, J64.pin6
  2LED2: R30.Pin_1, J64.pin7
  LEDCNTRL2: R31.Pin_0, J63.pin4
  LEDCNTRL4: R32.Pin_0, J63.pin3
  N27: Q10.B, R34.Pin_1, R35.Pin_1
  N28: Q10.C, R33.Pin_0
  ARDUINOLEDCNTRL: R35.Pin_0, J63.pin1
  N29: J64.pin1, R38.Pin_0
  N30: J64.pin2, R39.Pin_0
  N31: J64.pin3, R36.Pin_0
  N32: J64.pin4, R37.Pin_0
  Motor3AnalogOut: Motor3and4Out.pin4, MotorPotsToArduino.pin3
  Motor4AnalogOut: Motor3and4Out.pin9, MotorPotsToArduino.pin4
  Motor2AnalogOut: Motor1and2Out.pin2, MotorPotsToArduino.pin2
  Motor1AnalogOut: Motor1and2Out.pin7, MotorPotsToArduino.pin1
  Switch4: SWITCHES.pin1
  Switch2: SWITCHES.pin2
  Switch3: SWITCHES.pin3
  Switch1: SWITCHES.pin4
  N33: L7805ACV1.GND, R41.Pin_0, R42.Pin_0

notes:
  REMOVE 9V to PIN 1
