# Fritzing sketch TransistorTest (saved by Fritzing 0.9.3b)
breadboards: 1

parts:
  Q1 = PNP-Transistor [package="TO92 [THT]"]
  R1 = Resistor [tolerance=±5% resistance=100 package=THT]
  LED2 = LED - 5mm [color="Red (633nm)" package="5 mm [THT]"]
  D1 = Rectifier Diode [part_number=1N4001 package="300 mil [THT]"]
  D2 = Rectifier Diode [part_number=1N4001 package="300 mil [THT]"]
  D3 = Rectifier Diode [part_number=1N4001 package="300 mil [THT]"]
  D4 = Rectifier Diode [part_number=1N4001 package="300 mil [THT]"]
  Q2 = Basic FET N-Channel [package="TO220 [THT]"]  # not connected

nets:
  4.5V: Q1.E
  N1: Q1.B, D1.cathode, D2.cathode
  N2: Q1.C, R1.Pin_0
  N3: R1.Pin_1, LED2.anode
  N4: LED2.cathode, D3.anode, D4.anode
  9V: D1.anode, D3.cathode
  GND: D2.anode, D4.cathode
